// Logisim project bad_1_69.circ as structural Verilog: 1 circuit, main circuit main
module main (
  input  A,
  input  B,
  input  [2:0] C,
  output n7_Out1,
  output n3_Out,
  output [1:0] n5_Out0
);

  wire priority_encoder_1_out, undriven, undriven_4;
  wire [1:0] multiplexer_1_out, undriven_3;
  wire [2:0] bitadder_1_out, undriven_2;

  BitAdder #(.width(3)) bitadder_1 (.in0(undriven_2), .in1(undriven_2), .out(bitadder_1_out));
  Priority_Encoder #(.select(1)) priority_encoder_1 (
    .in0(B), .in1(A), .out(priority_encoder_1_out));  // open: gs, en_out, en_in
  // NAND_Gate n4_Out has open pins: in0=undriven_4, in1=undriven, out=open
  Multiplexer #(.select(1), .width(2), .enable("true")) multiplexer_1 (
    .in0(undriven_3), .in1(bitadder_1_out[1:0]), .out(multiplexer_1_out), .sel(bitadder_1_out[2]),
    .en(undriven_4));
  Decoder #(.select(2), .enable("false")) decoder_1 (
    .out1(n7_Out1), .sel(multiplexer_1_out));  // open: out0, out2, out3
endmodule
