// Logisim project bad_23_3.circ as structural Verilog: 1 circuit, main circuit main
module main (
  input  [3:0] A,
  input  B,
  input  C,
  input  D,
  output n2_Out0,
  output [1:0] n4_Prod,
  output n5_Sum
);

  wire demultiplexer_1_out2, demultiplexer_1_out3, n3_Out_p1, undriven, undriven_2, undriven_3;
  wire [1:0] n3_Out_p2, priority_encoder_1_out, undriven_4;

  Priority_Encoder #(.select(2)) priority_encoder_1 (
    .in0(undriven), .in1(undriven), .in2(B), .in3(D), .out(priority_encoder_1_out));  // open: gs, en_out, en_in
  Demultiplexer #(.select(2), .width(1), .enable("true")) demultiplexer_1 (
    .out0(n2_Out0), .out2(demultiplexer_1_out2), .out3(demultiplexer_1_out3), .in(undriven_2),
    .sel(undriven_4), .en(undriven_3));  // open: out1
  // XNOR_Gate #(.width(2), .\xor ("odd")) n3_Out: pin names not known; wires that end beside it: n3_Out_p1, n3_Out_p2
  Multiplier #(.width(2)) multiplier_1 (.a(undriven_4), .b(n3_Out_p2), .out(n4_Prod));  // open: cin, cout
  Adder #(.width(1)) adder_1 (
    .a(demultiplexer_1_out2), .b(demultiplexer_1_out3), .out(n5_Sum), .cin(undriven_3));  // open: cout
endmodule
