// Logisim project bad_303_17.circ as structural Verilog: 1 circuit, main circuit main
module main (
  input  A,
  input  [3:0] B,
  input  C,
  output n7_Out0
);

  wire n4_Out_out, n5_Out_out, priority_encoder_1_out, undriven, undriven_2, undriven_3, undriven_4;

  Priority_Encoder #(.select(1)) priority_encoder_1 (
    .in0(A), .in1(C), .out(priority_encoder_1_out));  // open: gs, en_out, en_in
  nand n4_Out (n4_Out_out, undriven_2, undriven);
  or n5_Out (n5_Out_out, undriven_3, n4_Out_out, priority_encoder_1_out);
  Decoder #(.select(1), .enable("true")) decoder_1 (.out0(n7_Out0), .sel(n5_Out_out), .en(undriven_4));  // open: out1
endmodule
