// Logisim project bad_33_1.circ as structural Verilog: 1 circuit, main circuit main
module main (
  input  A,
  input  [3:0] B,
  input  C,
  input  D,
  output n3_GS,
  output n5_Out1
);

  wire priority_encoder_1_gs;
  wire [1:0] priority_encoder_1_out;

  Priority_Encoder #(.select(2)) priority_encoder_1 (
    .in0(D), .in1(D), .in2(C), .in3(C), .out(priority_encoder_1_out), .gs(priority_encoder_1_gs));  // open: en_out, en_in
  Decoder #(.select(2), .enable("true")) decoder_1 (
    .out1(n5_Out1), .sel(priority_encoder_1_out), .en(priority_encoder_1_gs));  // open: out0, out2, out3
endmodule
