// Logisim project gt.circ as structural Verilog: 1 circuit, main circuit main
module main (
);

  // AND_Gate and_1 is placed but not wired
  // NAND_Gate nand_1 is placed but not wired
  Multiplexer #(.select(4), .width(4), .enable("true")) multiplexer_1 ();  // open: in0, in1, in2, in3, in4, in5, in6, in7, in8, in9, in10, in11, in12, in13, in14, in15, out, sel, en
  Decoder #(.select(2), .enable("true")) decoder_1 ();  // open: out0, out1, out2, out3, sel, en
  Priority_Encoder #(.select(4)) priority_encoder_1 ();  // open: in0, in1, in2, in3, in4, in5, in6, in7, in8, in9, in10, in11, in12, in13, in14, in15, out, gs, en_out, en_in
  Divider #(.width(4)) divider_1 ();  // open: a, b, out, upper, rem
  BitAdder #(.width(4)) bitadder_1 ();  // open: in0, out
  BitAdder #(.width(4)) bitadder_2 ();  // open: in0, in1, in2, in3, in4, in5, in6, out
  // AND_Gate and_2 is placed but not wired
  // NOR_Gate nor_1 is placed but not wired
  Demultiplexer #(.select(1), .width(4), .enable("true")) demultiplexer_1 ();  // open: out0, out1, in, sel, en
  Decoder #(.select(3), .enable("true")) decoder_2 ();  // open: out0, out1, out2, out3, out4, out5, out6, out7, sel, en
  BitSelector #(.width(8), .group(2)) bitselector_1 ();  // open: in, out, sel
  Negator #(.width(4)) negator_1 ();  // open: in, out
  BitAdder #(.width(4)) bitadder_3 ();  // open: in0, in1, out
  BitAdder #(.width(4)) bitadder_4 ();  // open: in0, in1, in2, in3, in4, in5, in6, in7, out
  // AND_Gate and_3 is placed but not wired
  // XOR_Gate xor_1 is placed but not wired
  Bit_Extender #(.in_width(8), .out_width(16), .\type ("zero")) bit_extender_1 ();  // open: in, out
  Demultiplexer #(.select(2), .width(4), .enable("true")) demultiplexer_2 ();  // open: out0, out1, out2, out3, in, sel, en
  Decoder #(.select(4), .enable("true")) decoder_3 ();  // open: out0, out1, out2, out3, out4, out5, out6, out7, out8, out9, out10, out11, out12, out13, out14, out15, sel, en
  BitSelector #(.width(8), .group(1)) bitselector_2 ();  // open: in, out, sel
  Comparator #(.width(4), .mode("unsigned")) comparator_1 ();  // open: a, b, gt, eq, lt
  BitAdder #(.width(4)) bitadder_5 ();  // open: in0, in1, in2, out
  LED led_1 ();  // open: in
  // AND_Gate and_4 is placed but not wired
  // XNOR_Gate xnor_1 is placed but not wired
  Multiplexer #(.select(1), .width(4), .enable("true")) multiplexer_2 ();  // open: in0, in1, out, sel, en
  Demultiplexer #(.select(3), .width(4), .enable("true")) demultiplexer_3 ();  // open: out0, out1, out2, out3, out4, out5, out6, out7, in, sel, en
  Priority_Encoder #(.select(1)) priority_encoder_2 ();  // open: in0, in1, out, gs, en_out, en_in
  Adder #(.width(4)) adder_1 ();  // open: a, b, out, cin, cout
  Shifter #(.width(4), .shift("ll")) shifter_1 ();  // open: in, dist, out
  BitAdder #(.width(4)) bitadder_6 ();  // open: in0, in1, in2, in3, out
  _7_Segment_Display u_7_segment_display_1 ();  // open: g, f, a, b, e, d, c, dp
  // NOT_Gate not_1 is placed but not wired
  // Odd_Parity odd_parity_1 is placed but not wired
  Multiplexer #(.select(2), .width(4), .enable("true")) multiplexer_3 ();  // open: in0, in1, in2, in3, out, sel, en
  Demultiplexer #(.select(4), .width(4), .enable("true")) demultiplexer_4 ();  // open: out0, out1, out2, out3, out4, out5, out6, out7, out8, out9, out10, out11, out12, out13, out14, out15, in, sel, en
  Priority_Encoder #(.select(2)) priority_encoder_3 ();  // open: in0, in1, in2, in3, out, gs, en_out, en_in
  Subtractor #(.width(4)) subtractor_1 ();  // open: a, b, out, bin, bout
  BitFinder #(.width(4), .\type ("low1")) bitfinder_1 ();  // open: in, index, found
  BitAdder #(.width(4)) bitadder_7 ();  // open: in0, in1, in2, in3, in4, out
  Hex_Digit_Display hex_digit_display_1 ();  // open: value, dp
  // Buffer buffer_1 is placed but not wired
  // Even_Parity even_parity_1 is placed but not wired
  Multiplexer #(.select(3), .width(4), .enable("true")) multiplexer_4 ();  // open: in0, in1, in2, in3, in4, in5, in6, in7, out, sel, en
  Decoder #(.select(1), .enable("true")) decoder_4 ();  // open: out0, out1, sel, en
  Priority_Encoder #(.select(3)) priority_encoder_4 ();  // open: in0, in1, in2, in3, in4, in5, in6, in7, out, en_in, gs, en_out
  Multiplier #(.width(4)) multiplier_1 ();  // open: a, b, out, cin, cout
  Adder #(.width(1)) adder_2 ();  // open: a, b, out, cin, cout
  BitAdder #(.width(4)) bitadder_8 ();  // open: in0, in1, in2, in3, in4, in5, out
endmodule
