// Logisim project rt.circ as structural Verilog: 1 circuit, main circuit main
module main (
  input  [1:0] A,
  input  B,
  input  [2:0] C,
  output n2_Out0
);

  wire undriven_3;
  wire [1:0] undriven, undriven_2;

  Subtractor #(.width(2)) subtractor_1 (.a(undriven), .b(undriven_2));  // open: out, bin, bout
  Demultiplexer #(.select(1), .width(1), .enable("false")) demultiplexer_1 (
    .out0(n2_Out0), .in(undriven_3), .sel(B));  // open: out1
endmodule
